# Fritzing sketch atmotest (saved by Fritzing 0.6.5b)
breadboards: 1

parts:
  Arduino1 = Arduino
  Power_plug1 = Power plug
  LED1 = LED - 5mm [color="Red (633nm)" package="5 mm [THT]"]
  LED2 = LED - 5mm [color="Green (555nm)" package="5 mm [THT]"]
  LED3 = LED - 5mm [color="Blue (430nm)" package="5 mm [THT]"]
  IC1 = ULN2803A [package=THT]

nets:
  GND: Arduino1.GND, Power_plug1.GND, IC1.0V
  N1: Arduino1.D11, IC1.In_1
  N2: Arduino1.D10, IC1.In_2
  N3: Arduino1.D9, IC1.In_3
  N4: Power_plug1.VCC, LED1.anode, LED2.anode, LED3.anode
  N5: LED1.cathode, IC1.Out_1
  N6: LED2.cathode, IC1.Out_2
  N7: LED3.cathode, IC1.Out_3
